// Digital circuit CPU.dig as structural Verilog
module CPU (
  input  RST,
  input  CLK,
  input  clk_2,
  input  CLK_SEL,
  input  nSTOP,
  output [7:0] opcode,
  output [15:0] rom,
  output [3:0] step
);

  wire A_LD, A_OE, A_SEL, addr_dec_1_p2, addr_dec_1_p3, alu_1_p14, alu_1_p15, alu_1_p16, alu_1_p17,
       alu_1_p18, ALU_CIN, ALU_S0, ALU_S1, ALU_S2, and_1_out, and_2_out, B_SET, C, CLK_t, FL_SEL, I, I_SET,
       I_WRITE, interrupts_1_p11, K_av, MAR_DIR, MEM_RD, MEM_WR, mmio_1_p10, N, nALU_OE, nFL_LD, nFL_OE,
       nHBA_OE, nIR_LD, nIRA_OE, nIRD_OE, nIRQ_CLR, nMAR_INC, nMAR_OE, nMARH_LD, nMARL_LD, nMMIO_CS,
       nMPC_RST, not_2_out, not_3_out, nPC_LD, nPCH_OE, nPCL_OE, nRST, nSHR, nSP_INC, nSP_LD, nSP_OE,
       nSPH_OE, nSPL_OE, nV_OE, nXY_AOE, nXY_INC, PC_INC, PC_OE, REG_LD, REG_OE, Rsrc, SHR_IN0, SP_DIR, V,
       V_B0, XY_DIR, Z;
  wire [3:0] mmio_1_p8;
  wire [7:0] mmio_1_p6, mmio_1_p9, pc_1_p10, rst_buffer_1_p2, rst_buffer_1_p3;
  wire [15:8] keyboard_1_d;
  wire [15:13] ctrlunit_1_p10;

  not not_1 (nRST, RST);
  and and_1 (and_1_out, CLK, ~CLK_SEL);  // And
  and and_2 (and_2_out, CLK_SEL, clk_2);
  or or_1 (CLK_t, and_1_out, and_2_out);
  // A_H__BUFFER a_h__buffer_1: pin names not known; wires that end beside it: nHBA_OE
  // RST_Buffer rst_buffer_1: pin names not known; wires that end beside it: nRST, rst_buffer_1_p2, {rst_buffer_1_p2, rst_buffer_1_p3}
  // ADDR_DEC addr_dec_1: pin names not known; wires that end beside it: {rst_buffer_1_p2, rst_buffer_1_p3}, addr_dec_1_p2, addr_dec_1_p3, nMMIO_CS
  // PC pc_1: pin names not known; wires that end beside it: {rst_buffer_1_p2, rst_buffer_1_p3}, PC_INC, nPC_LD, PC_OE, nPCL_OE, nPCH_OE, CLK_t, RST, {rst_buffer_1_p2, rst_buffer_1_p3}, pc_1_p10
  // SP sp_1: pin names not known; wires that end beside it: {rst_buffer_1_p2, rst_buffer_1_p3}, nSP_INC, SP_DIR, nSP_LD, nSP_OE, nSPH_OE, nSPL_OE, CLK_t
  not not_2 (not_2_out, nSTOP);
  not not_3 (not_3_out, K_av);
  // MAR mar_1: pin names not known; wires that end beside it: {rst_buffer_1_p2, rst_buffer_1_p3}, CLK_t, MAR_DIR, nMAR_INC, nMAR_OE, nMARH_LD, nMARL_LD, pc_1_p10, {rst_buffer_1_p2, rst_buffer_1_p3}, pc_1_p10
  // INTERRUPTS interrupts_1: pin names not known; wires that end beside it: not_2_out, 1'b1, not_3_out, I, nMPC_RST, nV_OE, V_B0, nIRQ_CLR, CLK_t, {rst_buffer_1_p2, rst_buffer_1_p3}, interrupts_1_p11
  RAMSinglePortSel #(.AddrBits(16), .Bits(8)) ramsingleportsel_1 (
    .A({rst_buffer_1_p2, rst_buffer_1_p3}), .CS(~addr_dec_1_p2), .WE(MEM_WR), .OE(MEM_RD), .D(pc_1_p10));
  EEPROM #(.AddrBits(15), .Bits(16)) eeprom_1 (
    .A({1'b0, rst_buffer_1_p2[5:0], rst_buffer_1_p3}), .CS(~addr_dec_1_p3), .WE(1'b0), .OE(MEM_RD), .D(rom));
  // RFILE rfile_1: pin names not known; wires that end beside it: pc_1_p10, opcode[2:0], Rsrc, REG_LD, REG_OE, nXY_INC, XY_DIR, nXY_AOE, CLK_t, RST, pc_1_p10, {rst_buffer_1_p2, rst_buffer_1_p3}, A_LD, A_OE
  // ALU alu_1: pin names not known; wires that end beside it: pc_1_p10, A_LD, A_OE, A_SEL, ALU_S0, ALU_S1, ALU_S2, nALU_OE, ALU_CIN, nSHR, SHR_IN0, CLK_t, RST, alu_1_p14, alu_1_p15, alu_1_p16, alu_1_p17, alu_1_p18, pc_1_p10
  // IR ir_1: pin names not known; wires that end beside it: rom, nIR_LD, nIRD_OE, nIRA_OE, CLK_t, opcode[7:3], opcode[2:0], Rsrc, pc_1_p10, rst_buffer_1_p3
  // microPC micropc_1: pin names not known; wires that end beside it: CLK_t, nMPC_RST, step
  // MMIO mmio_1: pin names not known; wires that end beside it: {rst_buffer_1_p2, rst_buffer_1_p3}, pc_1_p10, nMMIO_CS, MEM_WR, MEM_RD, mmio_1_p6, pc_1_p10, mmio_1_p8, mmio_1_p9, mmio_1_p10
  // FLAG_REG flag_reg_1: pin names not known; wires that end beside it: alu_1_p14, alu_1_p15, alu_1_p16, alu_1_p17, alu_1_p18, I_SET, I_WRITE, B_SET, nFL_OE, nFL_LD, FL_SEL, CLK_t, nRST, pc_1_p10, Z, C, N, V, I
  // CTRLUNIT ctrlunit_1: pin names not known; wires that end beside it: opcode, step, Z, C, N, V, interrupts_1_p11, {nMAR_INC, nMAR_OE, nMARH_LD, nMARL_LD, MEM_WR, MEM_RD, nMPC_RST, nHBA_OE, nIRA_OE, nIRD_OE, nIR_LD, nPCH_OE, nPCL_OE, PC_OE, nPC_LD, PC_INC}, {nFL_LD, nFL_OE, SHR_IN0, nSHR, ALU_CIN, nALU_OE, ALU_S2, ALU_S1, ALU_S0, A_SEL, nXY_AOE, XY_DIR, nXY_INC, REG_OE, REG_LD, MAR_DIR}, {ctrlunit_1_p10, V_B0, nV_OE, nIRQ_CLR, nSPH_OE, nSPL_OE, nSP_OE, nSP_LD, SP_DIR, nSP_INC, I_WRITE, I_SET, B_SET, FL_SEL}
  Keyboard keyboard_1 (.C(mmio_1_p10), .en(1'b1), .D({keyboard_1_d, mmio_1_p6}), .av(K_av));
  LED SCLK (.in(mmio_1_p8[0]));
  LED SDIN (.in(mmio_1_p8[1]));
  LED DC (.in(mmio_1_p8[2]));
  LED CS (.in(mmio_1_p8[3]));
  LED led_1 (.in(mmio_1_p9[0]));
  LED led_2 (.in(mmio_1_p9[1]));
  LED led_3 (.in(mmio_1_p9[2]));
  LED led_4 (.in(mmio_1_p9[3]));
  LED led_5 (.in(mmio_1_p9[4]));
  LED led_6 (.in(mmio_1_p9[5]));
  LED led_7 (.in(mmio_1_p9[6]));
  LED led_8 (.in(mmio_1_p9[7]));

  // Other names for the same wires on the sheet: Rdst[2:0] = opcode[2:0]

  // Notes on the sheet:
  //   clk_2: Hz: 10
  //   contents of eeprom_1 (hex, n*v repeats v):
  //   fb00,10ff,111f,5,dac0,da10,a800,d006,dac0,da11,ff00,610,744,2800
  //   ,e0c0,e000,ff00,10aa,11bb,dbc0,db16,ff00,ff00,16349*0,b,c0
endmodule
